# Fritzing sketch GrumpyWiFi (saved by Fritzing 0.9.4)
breadboards: 1

parts:
  ESP-01 = ESP8266 WiFi Module [part_number=ESP8266]
  OLED_I2C1 = OLED 128x64 I2C Monochrome Display
  S1 = Pushbutton [package="[SMD]"]
  Q2 = PNP-Transistor [package="TO92 [THT]"]
  LiPo_Battery = LIPO-110mAh [package=lipo-110]
  USB-Charge-Boost-module = Mini-USB _B_ connector with 5th pin broken out. [package=usb-micro_b]

nets:
  N1: ESP-01.VCC, ESP-01.CH_PD, Q2.C, USB-Charge-Boost-module.VBUS
  N2: ESP-01.GPIO_0, OLED_I2C1.SDA
  N3: ESP-01.RST, S1.Pin_3, S1.Pin_4
  N4: ESP-01.GPIO_2, OLED_I2C1.SCK
  GND: ESP-01.GND, OLED_I2C1.GND, S1.Pin_1, S1.Pin_2, USB-Charge-Boost-module.ID
  N5: ESP-01.TXD, Q2.B
  N6: OLED_I2C1.VDD, Q2.E
  N7: LiPo_Battery.+, USB-Charge-Boost-module.D-
  N8: LiPo_Battery.-, USB-Charge-Boost-module.GND

custom parts:
  ESP8266 WiFi Module: Generic WiFi Module based on the ESP8266 with onboard PCB antenna and UART communications
